# Fritzing sketch bluetooth (saved by Fritzing 0.9.2b)
breadboards: 1

parts:
  Part1 = Arduino Nano (Rev3.0)
  Part2 = Bluetooth HC-06

nets:
  N1: Part1.D1/TX, Part2.RXD
  N2: Part1.D0/RX, Part2.TXD
  GND: Part1.GND, Part2.GND
  5V: Part1.5V, Part2.VCC
