# Fritzing sketch led (saved by Fritzing 0.9.2b)
breadboards: 2

parts:
  LED1 = LED - 3mm [color="Red (633nm)" package="3 mm [THT]"]
  R1 = Resistor [tolerance=±5% resistance=220 package="0603 [SMD]"]
  Part1 = Arduino Nano (Rev3.0)

nets:
  N1: LED1.cathode, Part1.VIN
  N2: LED1.anode, R1.Pin_0
  N3: R1.Pin_1, Part1.D10
