# Fritzing sketch motor (saved by Fritzing 0.9.2b)
breadboards: 1

parts:
  Part1 = Arduino Nano (Rev3.0)
  Battery = LIPO-110mAh [package=lipo-110]
  Screw_Terminal_(B) = Screw terminal - 2 pins [package=THT]
  Screw_Terminal_(A) = Screw terminal - 2 pins [package=THT]  # not connected
  Left_Motor = DC Motor

nets:
  GND: Part1.GND, Battery.-
  B-1A: Part1.D6
  B-1B: Part1.D7
  VCC: Battery.+
  N1: Screw_Terminal_(B).pin1, Left_Motor.pin_1
  N2: Screw_Terminal_(B).pin2, Left_Motor.pin_2
