# Fritzing sketch servo (saved by Fritzing 0.9.2b)
breadboards: 1

parts:
  Part1 = Arduino Nano (Rev3.0)
  J1 = Basic Servo

nets:
  GND: Part1.GND, J1.gnd
  N1: Part1.D3, J1.pulse
  5V: Part1.5V, J1.vcc
