# Fritzing sketch temperature-lm35 (saved by Fritzing 0.9.2b)
breadboards: 1

parts:
  Part1 = Arduino Uno (Rev3)
  T1 = LM35 Temperature Sensor [package="TO92 [THT]"]
  LED1 = RGB LED (com. cathode, rbg) [package="5 mm [THT]"]
  R1 = Resistor [tolerance=±5% resistance=220 package="1206 [SMD]"]
  R2 = Resistor [tolerance=±5% resistance=220 package="1206 [SMD]"]
  R3 = Resistor [tolerance=±5% resistance=220 package="1206 [SMD]"]

nets:
  N1: Part1.A0, T1.Vout
  N2: Part1.D3_PWM, R3.Pin_0
  N3: Part1.D5_PWM, R1.Pin_0
  N4: Part1.D6_PWM, R2.Pin_0
  N5: Part1.5V, T1.+Vs
  GND: Part1.GND, T1.GND, LED1.common_cathode
  N6: LED1.red_anode, R3.Pin_1
  N7: LED1.blue_anode, R2.Pin_1
  N8: LED1.green_anode, R1.Pin_1
