# Fritzing sketch full_bot (saved by Fritzing 0.9.2b)
breadboards: 1

parts:
  Part1 = Arduino Nano (Rev3.0)
  LIPO_3_7V_Battery_(R=VCC_B=GND) = LIPO-110mAh [package=lipo-110]
  Screw_Terminal_(B) = Screw terminal - 2 pins [package=THT]
  Right_Motor = DC Motor
  Screw_Terminal_(A) = Screw terminal - 2 pins [package=THT]
  Left_Motor = DC Motor
  Servo2 = Basic Servo
  Servo1 = Basic Servo
  LED = LED - 5mm [color="Red (633nm)" package="5 mm [THT]"]
  Resistor = Resistor [tolerance=±5% resistance=220 package=THT]

nets:
  BT RX: Part1.D1/TX
  BT TX: Part1.D0/RX
  BT GND/GND: Part1.GND, LIPO_3_7V_Battery_(R=VCC_B=GND).-, Servo2.gnd, Servo1.gnd, LED.cathode
  N1: Part1.D3, Servo1.pulse
  N2: Part1.D4, Servo2.pulse
  B-1A: Part1.D6
  B-1B: Part1.D7
  A-1B: Part1.D8
  A-1A: Part1.D9
  N3: Part1.D11/MOSI, Resistor.Pin_0
  BT VCC/VCC: Part1.5V, LIPO_3_7V_Battery_(R=VCC_B=GND).+, Servo2.vcc, Servo1.vcc
  N4: Screw_Terminal_(B).pin1, Left_Motor.pin_1
  N5: Screw_Terminal_(B).pin2, Left_Motor.pin_2
  N6: Right_Motor.pin_1, Screw_Terminal_(A).pin1
  N7: Right_Motor.pin_2, Screw_Terminal_(A).pin2
  N8: LED.anode, Resistor.Pin_1

notes:
  Motor controller pins
